# Fritzing sketch shift registor test (saved by Fritzing 0.9.2b)
breadboards: 1

parts:
  U1 = 74HC595 [package="DIP16 [THT]"]
  IC1 = PICAXE-20M [package=THT]
  LED1 = smd LED [color="Red (633nm)" package="0805 [SMD]"]
  LED2 = smd LED [color="Red (633nm)" package="0805 [SMD]"]
  LED3 = smd LED [color="Red (633nm)" package="0805 [SMD]"]
  LED4 = smd LED [color="Red (633nm)" package="0805 [SMD]"]
  LED5 = smd LED [color="Red (633nm)" package="0805 [SMD]"]
  LED6 = smd LED [color="Red (633nm)" package="0805 [SMD]"]
  LED7 = smd LED [color="Red (633nm)" package="0805 [SMD]"]
  LED8 = smd LED [color="Red (633nm)" package="0805 [SMD]"]
  LED9 = smd LED [color="Red (633nm)" package="0805 [SMD]"]
  LED10 = smd LED [color="Red (633nm)" package="0805 [SMD]"]
  LED11 = smd LED [color="Red (633nm)" package="0805 [SMD]"]
  LED12 = smd LED [color="Red (633nm)" package="0805 [SMD]"]
  LED13 = smd LED [color="Red (633nm)" package="0805 [SMD]"]
  LED14 = smd LED [color="Red (633nm)" package="0805 [SMD]"]
  LED15 = smd LED [color="Red (633nm)" package="0805 [SMD]"]
  LED16 = smd LED [color="Red (633nm)" package="0805 [SMD]"]
  R1 = 10k Ω Resistor [package=THT]
  Part1 = Bluetooth HC-05 Macho

nets:
  N1: U1.Q1, LED4.anode
  N2: U1.Q2, LED6.anode
  N3: U1.Q3, LED8.anode
  N4: U1.Q4, LED10.anode
  N5: U1.Q5, LED12.anode
  N6: U1.Q6, LED15.anode
  N7: U1.Q7, LED16.anode
  GND: U1.GND, IC1.0V, LED1.cathode, LED3.cathode, LED5.cathode, LED7.cathode, LED9.cathode, LED11.cathode, LED13.cathode, LED14.cathode, R1.Pin_0, Part1.GND
  N8: U1.SH_CP, IC1.In_1_/_ADC_1
  N9: U1.ST_CP, IC1.In_2_/_ADC_2
  N10: U1.DS, IC1.In_0_/_Infrain
  N11: U1.Q0, LED2.anode
  VCC: U1.VCC, IC1.+V, Part1.VCC
  N12: IC1.Serial_In, R1.Pin_1
  N13: IC1.Out_4, Part1.RXD
  N14: IC1.Out_3, Part1.State
  N15: LED1.anode, LED2.cathode
  N16: LED3.anode, LED4.cathode
  N17: LED5.anode, LED6.cathode
  N18: LED7.anode, LED8.cathode
  N19: LED9.anode, LED10.cathode
  N20: LED11.anode, LED12.cathode
  N21: LED13.anode, LED15.cathode
  N22: LED14.anode, LED16.cathode

custom parts:
  10k Ω Resistor: A generic resistor (0.25W)
